# Fritzing sketch projetoTCCFTZ (saved by Fritzing 0.9.10b)
breadboards: 1

parts:
  Componente1 = Arduino Mega 2560 (Rev3)
  Componente4 = Soil Moisture Sensor
  microSD1 = MicroSD Card Module
  Componente3 = Soil Moisture Sensor
  Componente2 = Soil Moisture Sensor
  U2 = RELAY [package=relay-jzc]
  U3 = RELAY [package=relay-jzc]
  Componente5 = Soil Moisture Sensor
  R2 = Resistor [tolerance=±5% power=0.25 resistance=220 package=THT]  # not connected
  R4 = Resistor [tolerance=±5% power=0.25 resistance=220 package=THT]  # not connected
  R6 = Resistor [tolerance=±5% power=0.25 resistance=220 package=THT]  # not connected
  R8 = Resistor [tolerance=±5% resistance=330 package="1206 [SMD]"]
  R9 = Resistor [tolerance=±5% resistance=330 package="1206 [SMD]"]
  R10 = Resistor [tolerance=±5% resistance=330 package="1206 [SMD]"]

nets:
  N1: Componente1.A0, Componente4.SIG
  N2: Componente1.A1, Componente5.SIG
  N3: Componente1.A2, Componente3.SIG
  N4: Componente1.A3, Componente2.SIG
  N5: Componente1.D11_PWM, U3.COIL2
  N6: Componente1.D10_PWM, U2.COIL2
  VCC: Componente1.5V, Componente4.VCC, microSD1.VCC, Componente3.VCC, Componente2.VCC, U2.NC, U3.NC
  GND: Componente1.GND, Componente4.GND, microSD1.GND, Componente3.GND, Componente2.GND, U2.NO, U3.NO, Componente5.GND, R8.Pin_1, R9.Pin_1, R10.Pin_1
  N7: Componente1.D50, microSD1.MISO
  N8: microSD1.MOSI, R9.Pin_0
  N9: microSD1.SCK, R10.Pin_0
  N10: microSD1.CS, R8.Pin_0

// code stored in the sketch: onLed.ino
const int buton=3;
volatile int sayac = 0;
volatile unsigned long sure=300;
const int INTbuton = 1; //interrupt1-INT1 Uno için Buton Pin3
void setup() {
  // put your setup code here, to run once:
pinMode(buton,INPUT);
for(int i=4;i<14;i++){
pinMode(i,OUTPUT);
}
attachInterrupt(INTbuton, sureDegistir, RISING);
}
void sureDegistir() {
  if (sayac < 5) {
    sayac = sayac + 1;
  }
  else {
    sayac = 1;
  }
  if (sayac == 1) {
    sure = 300;
  }
  if (sayac == 2) {
    sure = 700;
  }
  if (sayac == 3) {
    sure = 1000;
  }
  if (sayac == 4) {
    sure = 1500;
  }
  if (sayac == 5) {
    sure = 2000;
  }
}
unsigned long t0=0; //ba?lang?ç zaman?
unsigned long t1;
unsigned long t2;
unsigned long t3;
unsigned long t4;
unsigned long t5;
unsigned long t6;
unsigned long t7;
unsigned long t8;
unsigned long t9;
unsigned long t10;
unsigned long t11;
unsigned long t12;
unsigned long t13;
unsigned long t14;
unsigned long t15;
unsigned long t16;
unsigned long t17;
unsigned long t18;
unsigned long t19;
unsigned long t20;
void loop() {
  unsigned long sureAralik;

do{
  t1=millis();
  sureAralik=t1-t0;
  }
while(sureAralik<sure);
digitalWrite(4,1);

do{
  t2=millis();
  sureAralik=t2-t1;
  }
while(sureAralik<sure);
digitalWrite(5,1);

do{
  t3=millis();
  sureAralik=t3-t2;
  }
while(sureAralik<sure);
digitalWrite(6,1);

do{
  t4=millis();
  sureAralik=t4-t3;
  }
while(sureAralik<sure);
digitalWrite(7,1);


do{
  t5=millis();
  sureAralik=t5-t4;
  }
while(sureAralik<sure);
digitalWrite(8,1);

do{
  t6=millis();
  sureAralik=t6-t5;
  }
while(sureAralik<sure);
digitalWrite(9,1);

do{
  t7=millis();
  sureAralik=t7-t6;
  }
while(sureAralik<sure);
digitalWrite(10,1);

do{
  t8=millis();
  sureAralik=t8-t7;
  }
while(sureAralik<sure);
digitalWrite(11,1);

do{
  t9=millis();
  sureAralik=t9-t8;
  }
while(sureAralik<sure);
digitalWrite(12,1);

do{
  t10=millis();
  sureAralik=t10-t9;
  }
while(sureAralik<sure);
digitalWrite(13,1);

do{
  t11=millis();
  sureAralik=t11-t10;
  }
while(sureAralik<sure);
digitalWrite(4,0);

do{
  t12=millis();
  sureAralik=t12-t11;
  }
while(sureAralik<sure);
digitalWrite(5,0);

do{
  t13=millis();
  sureAralik=t13-t12;
  }
while(sureAralik<sure);
digitalWrite(6,0);

do{
  t14=millis();
  sureAralik=t14-t13;
  }
while(sureAralik<sure);
digitalWrite(7,0);


do{
  t15=millis();
  sureAralik=t15-t14;
  }
while(sureAralik<sure);
digitalWrite(8,0);

do{
  t16=millis();
  sureAralik=t16-t15;
  }
while(sureAralik<sure);
digitalWrite(9,0);

do{
  t17=millis();
  sureAralik=t17-t16;
  }
while(sureAralik<sure);
digitalWrite(10,0);

do{
  t18=millis();
  sureAralik=t18-t17;
  }
while(sureAralik<sure);
digitalWrite(11,0);

do{
  t19=millis();
  sureAralik=t19-t18;
  }
while(sureAralik<sure);
digitalWrite(12,0);

do{
  t20=millis();
  sureAralik=t20-t19;
  }
while(sureAralik<sure);
digitalWrite(13,0);

}
